// Logisim project stack_logical_normal.circ as structural Verilog: 22 circuits, main circuit main
module main (
  input  CLK,
  input  RESET,
  input  [1:0] COMMAND,
  input  [2:0] INDEX,
  input  [3:0] IO_DATA_in,
  output [3:0] IO_DATA_out
);

  wire [3:0] stack_1_d0, stack_1_d1, stack_1_d2, stack_1_d3, stack_1_d4;

  // Probe on stack_1_d0
  stack stack_1 (
    .CLK(CLK), .RESET(RESET), .COMMAND(COMMAND), .INDEX(INDEX), .IO_DATA_in(IO_DATA_in), .d0(stack_1_d0),
    .d1(stack_1_d1), .d2(stack_1_d2), .d3(stack_1_d3), .d4(stack_1_d4), .IO_DATA_out(IO_DATA_out));
  // Probe on stack_1_d1
  // Probe on stack_1_d2
  // Probe on stack_1_d3
  // Probe on stack_1_d4
endmodule

module stack (
  input  CLK,
  input  RESET,
  input  [1:0] COMMAND,
  input  [2:0] INDEX,
  input  [3:0] IO_DATA_in,
  output [3:0] d0,
  output [3:0] d1,
  output [3:0] d2,
  output [3:0] d3,
  output [3:0] d4,
  output [3:0] IO_DATA_out
);

  wire and_1_out, not_1_out, not_2_out;
  wire [3:0] transmission_1_p1;

  not not_1 (not_1_out, COMMAND[1]);
  and and_1 (and_1_out, COMMAND[0], not_1_out);
  not not_2 (not_2_out, and_1_out);
  // Transmission_Gate #(.width(4)) transmission_1: pin names not known; wires that end beside it: transmission_1_p1, and_1_out, not_2_out, IO_DATA_in
  sub_stack sub_stack_1 (
    .CLK(CLK), .RESET(RESET), .COMMAND(COMMAND), .INDEX(INDEX), .I_DATA(IO_DATA_in), .d0(d0), .d1(d1),
    .d2(d2), .d3(d3), .d4(d4), .O_DATA(transmission_1_p1));

  assign IO_DATA_out = IO_DATA_in;

  // Notes on the sheet:
  //   your circuit must be here
endmodule

module rs_D (
  input  R,
  input  S,
  input  RESET,
  output Q,
  output NQ
);

  wire nor_2_out, por_1_out;

  nor nor_1 (Q, R, NQ);
  nor nor_2 (nor_2_out, Q, S);
  or or_1 (NQ, nor_2_out, por_1_out, RESET);
  POR por_1 (.out(por_1_out));
endmodule

module sync_rs_D (
  input  R,
  input  CLK,
  input  S,
  input  RESET,
  output Q,
  output NQ
);

  wire and_1_out, and_2_out;

  and and_1 (and_1_out, R, CLK);
  and and_2 (and_2_out, CLK, S);
  rs_D rs_d_1 (.R(and_1_out), .S(and_2_out), .RESET(RESET), .Q(Q), .NQ(NQ));
endmodule

module D_trigger (
  input  CLK,
  input  D,
  input  RESET,
  output Q,
  output NQ
);

  wire not_1_out;

  not not_1 (not_1_out, D);
  sync_rs_D sync_rs_d_1 (.R(not_1_out), .CLK(CLK), .S(D), .RESET(RESET), .Q(Q), .NQ(NQ));
endmodule

module new_and (
  input  KEY,
  input  [3:0] I_DATA,
  output [3:0] RESULT
);

  and and_1 (RESULT[0], I_DATA[0], KEY);
  and and_2 (RESULT[1], I_DATA[1], KEY);
  and and_3 (RESULT[2], I_DATA[2], KEY);
  and and_4 (RESULT[3], I_DATA[3], KEY);
endmodule

module result (
  input  [3:0] d0,
  input  [3:0] d1,
  input  [3:0] d2,
  input  [3:0] d3,
  input  [3:0] d4,
  output [3:0] RES
);

  or or_1 (RES[0], d0[0], d1[0], d2[0], d3[0], d4[0]);
  or or_2 (RES[1], d0[1], d1[1], d2[1], d3[1], d4[1]);
  or or_3 (RES[2], d0[2], d1[2], d2[2], d3[2], d4[2]);
  or or_4 (RES[3], d0[3], d1[3], d2[3], d3[3], d4[3]);
endmodule

module check0 (
  input  [2:0] IN_DATA,
  output O_DATA
);

  wire not_1_out, not_2_out, not_3_out;

  not not_1 (not_1_out, IN_DATA[0]);
  not not_2 (not_2_out, IN_DATA[1]);
  not not_3 (not_3_out, IN_DATA[2]);
  and and_1 (O_DATA, not_1_out, not_2_out, not_3_out);
endmodule

module check1 (
  input  [2:0] IN_DATA,
  output O_DATA
);

  wire not_1_out, not_2_out;

  not not_1 (not_1_out, IN_DATA[1]);
  not not_2 (not_2_out, IN_DATA[2]);
  and and_1 (O_DATA, IN_DATA[0], not_1_out, not_2_out);
endmodule

module check2 (
  input  [2:0] IN_DATA,
  output O_DATA
);

  wire not_1_out, not_2_out;

  not not_1 (not_1_out, IN_DATA[0]);
  not not_2 (not_2_out, IN_DATA[2]);
  and and_1 (O_DATA, not_1_out, IN_DATA[1], not_2_out);
endmodule

module check3 (
  input  [2:0] IN_DATA,
  output O_DATA
);

  wire not_1_out;

  not not_1 (not_1_out, IN_DATA[2]);
  and and_1 (O_DATA, IN_DATA[0], IN_DATA[1], not_1_out);
endmodule

module check4 (
  input  [2:0] IN_DATA,
  output O_DATA
);

  wire not_1_out, not_2_out;

  not not_1 (not_1_out, IN_DATA[0]);
  not not_2 (not_2_out, IN_DATA[1]);
  and and_1 (O_DATA, not_1_out, not_2_out, IN_DATA[2]);
endmodule

module memory4bit (
  input  CLK,
  input  KEY,
  input  RESET,
  input  [3:0] I_DATA,
  output [3:0] O_DATA
);

  wire and_1_out;

  and and_1 (and_1_out, CLK, KEY);
  D_trigger d_trigger_1 (.CLK(and_1_out), .D(I_DATA[0]), .RESET(RESET), .Q(O_DATA[0]));  // open: NQ
  D_trigger d_trigger_2 (.CLK(and_1_out), .D(I_DATA[1]), .RESET(RESET), .Q(O_DATA[1]));  // open: NQ
  D_trigger d_trigger_3 (.CLK(and_1_out), .D(I_DATA[2]), .RESET(RESET), .Q(O_DATA[2]));  // open: NQ
  D_trigger d_trigger_4 (.CLK(and_1_out), .D(I_DATA[3]), .RESET(RESET), .Q(O_DATA[3]));  // open: NQ
endmodule

module \checker  (
  input  AND1,
  input  AND2,
  input  OR1,
  output RESULT
);

  wire and_1_out;

  and and_1 (and_1_out, AND1, AND2);
  or or_1 (RESULT, and_1_out, OR1);
endmodule

module rs_JK (
  input  R,
  input  S,
  input  RESET,
  output Q,
  output NQ
);

  wire nor_1_out, por_1_out;

  nor nor_1 (nor_1_out, R, NQ);
  POR por_1 (.out(por_1_out));
  nor nor_2 (NQ, Q, S);
  or or_1 (Q, nor_1_out, por_1_out, RESET);
endmodule

module sync_rs_JK (
  input  R,
  input  CLK,
  input  S,
  input  RESET,
  output Q,
  output NQ
);

  wire and_1_out, and_2_out;

  and and_1 (and_1_out, R, CLK);
  and and_2 (and_2_out, CLK, S);
  rs_JK rs_jk_1 (.R(and_1_out), .S(and_2_out), .RESET(RESET), .Q(Q), .NQ(NQ));
endmodule

module JK_trigger (
  input  K,
  input  CLK,
  input  J,
  input  RESET,
  output Q,
  output NQ
);

  wire and_1_out, and_2_out, not_1_out, sync_rs_jk_1_nq, sync_rs_jk_1_q;

  and and_1 (and_1_out, Q, K);
  and and_2 (and_2_out, J, NQ);
  sync_rs_JK sync_rs_jk_1 (
    .R(and_1_out), .CLK(CLK), .S(and_2_out), .RESET(RESET), .Q(sync_rs_jk_1_q), .NQ(sync_rs_jk_1_nq));
  not not_1 (not_1_out, CLK);
  sync_rs_JK sync_rs_jk_2 (.R(sync_rs_jk_1_nq), .CLK(not_1_out), .S(sync_rs_jk_1_q), .RESET(RESET), .Q(Q), .NQ(NQ));
endmodule

module indicator (
  input  CLK,
  input  RESET,
  output [2:0] O_DATA
);

  wire and_1_out, not_1_out, or_1_out;

  or or_1 (or_1_out, RESET, and_1_out);
  JK_trigger jk_trigger_1 (.K(1'b1), .CLK(CLK), .J(1'b1), .RESET(or_1_out), .NQ(O_DATA[0]));  // open: Q
  JK_trigger jk_trigger_2 (.K(1'b1), .CLK(O_DATA[0]), .J(1'b1), .RESET(or_1_out), .NQ(O_DATA[1]));  // open: Q
  JK_trigger jk_trigger_3 (.K(1'b1), .CLK(O_DATA[1]), .J(1'b1), .RESET(or_1_out), .NQ(O_DATA[2]));  // open: Q
  not not_1 (not_1_out, O_DATA[1]);
  and and_1 (and_1_out, O_DATA[0], not_1_out, O_DATA[2]);
endmodule

module convertor (
  input  [2:0] ELEMENT1,
  input  [2:0] ELEMENT2,
  output [2:0] O_DATA
);

  wire and_1_out, and_2_out, and_3_out, and_4_out, and_5_out, and_6_out, and_7_out, and_8_out, and_9_out,
       and_10_out, and_11_out, and_12_out, and_13_out, and_14_out, and_15_out, and_16_out, and_17_out,
       and_18_out, and_19_out, and_20_out, and_21_out, and_22_out, and_23_out, and_24_out, and_25_out,
       and_26_out, and_27_out, and_28_out, and_29_out, and_30_out, and_31_out, and_32_out, and_33_out,
       and_34_out, and_35_out, and_36_out, and_37_out, and_38_out, and_39_out, and_40_out, check0_1_o_data,
       check0_2_o_data, check1_1_o_data, check1_2_o_data, check2_1_o_data, check2_2_o_data, check3_1_o_data,
       check3_2_o_data, check4_1_o_data, check4_2_o_data, not_1_out, not_2_out, not_3_out, not_4_out,
       not_5_out, not_6_out, not_7_out, not_8_out, not_9_out, not_10_out, or_1_out, or_2_out, or_3_out,
       or_4_out, or_5_out;

  check0 check0_1 (.IN_DATA(ELEMENT1), .O_DATA(check0_1_o_data));
  check1 check1_1 (.IN_DATA(ELEMENT1), .O_DATA(check1_1_o_data));
  check2 check2_1 (.IN_DATA(ELEMENT1), .O_DATA(check2_1_o_data));
  check3 check3_1 (.IN_DATA(ELEMENT1), .O_DATA(check3_1_o_data));
  check4 check4_1 (.IN_DATA(ELEMENT1), .O_DATA(check4_1_o_data));
  check0 check0_2 (.IN_DATA(ELEMENT2), .O_DATA(check0_2_o_data));
  check1 check1_2 (.IN_DATA(ELEMENT2), .O_DATA(check1_2_o_data));
  check2 check2_2 (.IN_DATA(ELEMENT2), .O_DATA(check2_2_o_data));
  check3 check3_2 (.IN_DATA(ELEMENT2), .O_DATA(check3_2_o_data));
  check4 check4_2 (.IN_DATA(ELEMENT2), .O_DATA(check4_2_o_data));
  and and_1 (and_1_out, check0_1_o_data, check0_2_o_data);
  and and_2 (and_2_out, check0_1_o_data, check1_2_o_data);
  and and_3 (and_3_out, check0_1_o_data, check2_2_o_data);
  and and_4 (and_4_out, check0_1_o_data, check3_2_o_data);
  and and_5 (and_5_out, check0_1_o_data, check4_2_o_data);
  and and_6 (and_6_out, check1_1_o_data, check0_2_o_data);
  and and_7 (and_7_out, check1_1_o_data, check1_2_o_data);
  and and_8 (and_8_out, check1_1_o_data, check2_2_o_data);
  and and_9 (and_9_out, check1_1_o_data, check3_2_o_data);
  and and_10 (and_10_out, check1_1_o_data, check4_2_o_data);
  and and_11 (and_11_out, check2_1_o_data, check0_2_o_data);
  and and_12 (and_12_out, check2_1_o_data, check1_2_o_data);
  and and_13 (and_13_out, check2_1_o_data, check2_2_o_data);
  and and_14 (and_14_out, check2_1_o_data, check3_2_o_data);
  and and_15 (and_15_out, check2_1_o_data, check4_2_o_data);
  and and_16 (and_16_out, check3_1_o_data, check0_2_o_data);
  and and_17 (and_17_out, check3_1_o_data, check1_2_o_data);
  and and_18 (and_18_out, check3_1_o_data, check2_2_o_data);
  and and_19 (and_19_out, check3_1_o_data, check3_2_o_data);
  and and_20 (and_20_out, check3_1_o_data, check4_2_o_data);
  and and_21 (and_21_out, check4_1_o_data, check0_2_o_data);
  and and_22 (and_22_out, check4_1_o_data, check1_2_o_data);
  and and_23 (and_23_out, check4_1_o_data, check2_2_o_data);
  and and_24 (and_24_out, check4_1_o_data, check3_2_o_data);
  and and_25 (and_25_out, check4_1_o_data, check4_2_o_data);
  or or_1 (or_1_out, and_1_out, and_7_out, and_13_out, and_19_out, and_25_out);
  or or_2 (or_2_out, and_5_out, and_6_out, and_12_out, and_18_out, and_24_out);
  or or_3 (or_3_out, and_4_out, and_10_out, and_11_out, and_17_out, and_23_out);
  or or_4 (or_4_out, and_3_out, and_9_out, and_15_out, and_16_out, and_22_out);
  or or_5 (or_5_out, and_2_out, and_8_out, and_14_out, and_20_out, and_21_out);
  not not_1 (not_1_out, 1'b1);
  not not_2 (not_2_out, 1'b1);
  not not_3 (not_3_out, 1'b1);
  not not_4 (not_4_out, 1'b1);
  not not_5 (not_5_out, 1'b1);
  not not_6 (not_6_out, 1'b1);
  not not_7 (not_7_out, 1'b1);
  not not_8 (not_8_out, 1'b1);
  not not_9 (not_9_out, 1'b1);
  not not_10 (not_10_out, 1'b1);
  and and_26 (and_26_out, not_1_out, or_1_out);
  and and_27 (and_27_out, not_2_out, or_1_out);
  and and_28 (and_28_out, not_3_out, or_1_out);
  and and_29 (and_29_out, 1'b1, or_2_out);
  and and_30 (and_30_out, not_4_out, or_2_out);
  and and_31 (and_31_out, not_5_out, or_2_out);
  and and_32 (and_32_out, not_6_out, or_3_out);
  and and_33 (and_33_out, 1'b1, or_3_out);
  and and_34 (and_34_out, not_7_out, or_3_out);
  and and_35 (and_35_out, 1'b1, or_4_out);
  and and_36 (and_36_out, 1'b1, or_4_out);
  and and_37 (and_37_out, not_8_out, or_4_out);
  and and_38 (and_38_out, not_9_out, or_5_out);
  and and_39 (and_39_out, not_10_out, or_5_out);
  and and_40 (and_40_out, 1'b1, or_5_out);
  or or_6 (O_DATA[0], and_26_out, and_29_out, and_32_out, and_35_out, and_38_out);
  or or_7 (O_DATA[1], and_27_out, and_30_out, and_33_out, and_36_out, and_39_out);
  or or_8 (O_DATA[2], and_28_out, and_31_out, and_34_out, and_37_out, and_40_out);
endmodule

module convertor_minus (
  input  [2:0] I_DATA,
  output [2:0] O_DATA
);

  wire and_1_out, and_2_out, and_3_out, and_4_out, and_5_out, and_6_out, and_7_out, and_8_out, and_9_out,
       and_10_out, and_11_out, and_12_out, and_13_out, and_14_out, and_15_out, check0_1_o_data,
       check1_1_o_data, check2_1_o_data, check3_1_o_data, check4_1_o_data, not_1_out, not_2_out, not_3_out,
       not_4_out, not_5_out, not_6_out, not_7_out, not_8_out, not_9_out, not_10_out;

  check0 check0_1 (.IN_DATA(I_DATA), .O_DATA(check0_1_o_data));
  check1 check1_1 (.IN_DATA(I_DATA), .O_DATA(check1_1_o_data));
  check2 check2_1 (.IN_DATA(I_DATA), .O_DATA(check2_1_o_data));
  check3 check3_1 (.IN_DATA(I_DATA), .O_DATA(check3_1_o_data));
  check4 check4_1 (.IN_DATA(I_DATA), .O_DATA(check4_1_o_data));
  not not_1 (not_1_out, 1'b1);
  not not_2 (not_2_out, 1'b1);
  not not_3 (not_3_out, 1'b1);
  not not_4 (not_4_out, 1'b1);
  not not_5 (not_5_out, 1'b1);
  not not_6 (not_6_out, 1'b1);
  not not_7 (not_7_out, 1'b1);
  not not_8 (not_8_out, 1'b1);
  not not_9 (not_9_out, 1'b1);
  not not_10 (not_10_out, 1'b1);
  and and_1 (and_1_out, not_1_out, check0_1_o_data);
  and and_2 (and_2_out, not_2_out, check0_1_o_data);
  and and_3 (and_3_out, not_3_out, check0_1_o_data);
  and and_4 (and_4_out, 1'b1, check1_1_o_data);
  and and_5 (and_5_out, not_4_out, check1_1_o_data);
  and and_6 (and_6_out, not_5_out, check1_1_o_data);
  and and_7 (and_7_out, not_6_out, check2_1_o_data);
  and and_8 (and_8_out, 1'b1, check2_1_o_data);
  and and_9 (and_9_out, not_7_out, check2_1_o_data);
  and and_10 (and_10_out, 1'b1, check3_1_o_data);
  and and_11 (and_11_out, 1'b1, check3_1_o_data);
  and and_12 (and_12_out, not_8_out, check3_1_o_data);
  and and_13 (and_13_out, not_9_out, check4_1_o_data);
  and and_14 (and_14_out, not_10_out, check4_1_o_data);
  and and_15 (and_15_out, 1'b1, check4_1_o_data);
  or or_1 (O_DATA[0], and_1_out, and_4_out, and_7_out, and_10_out, and_13_out);
  or or_2 (O_DATA[1], and_2_out, and_5_out, and_8_out, and_11_out, and_14_out);
  or or_3 (O_DATA[2], and_3_out, and_6_out, and_9_out, and_12_out, and_15_out);
endmodule

module module5 (
  input  [2:0] I_DATA,
  output [2:0] O_DATA
);

  wire and_1_out, and_2_out, and_3_out, and_4_out, and_5_out, and_6_out, and_7_out, and_8_out, and_9_out,
       and_10_out, and_11_out, and_12_out, and_13_out, and_14_out, and_15_out, and_16_out, and_17_out,
       and_18_out, check0_1_o_data, check1_1_o_data, check2_1_o_data, check3_1_o_data, check4_1_o_data,
       not_1_out, not_2_out, not_3_out, not_4_out, not_5_out, not_6_out, not_7_out, not_8_out, not_9_out,
       not_10_out, not_11_out, not_12_out, or_1_out, or_2_out, or_3_out;

  not not_1 (not_1_out, I_DATA[1]);
  not not_2 (not_2_out, I_DATA[0]);
  and and_1 (and_1_out, I_DATA[0], not_1_out, I_DATA[2]);
  and and_2 (and_2_out, not_2_out, I_DATA[1], I_DATA[2]);
  and and_3 (and_3_out, I_DATA[0], I_DATA[1], I_DATA[2]);
  check0 check0_1 (.IN_DATA(I_DATA), .O_DATA(check0_1_o_data));
  check1 check1_1 (.IN_DATA(I_DATA), .O_DATA(check1_1_o_data));
  check2 check2_1 (.IN_DATA(I_DATA), .O_DATA(check2_1_o_data));
  or or_1 (or_1_out, check0_1_o_data, and_1_out);
  or or_2 (or_2_out, check1_1_o_data, and_2_out);
  or or_3 (or_3_out, check2_1_o_data, and_3_out);
  check3 check3_1 (.IN_DATA(I_DATA), .O_DATA(check3_1_o_data));
  check4 check4_1 (.IN_DATA(I_DATA), .O_DATA(check4_1_o_data));
  not not_3 (not_3_out, 1'b1);
  not not_4 (not_4_out, 1'b1);
  not not_5 (not_5_out, 1'b1);
  not not_6 (not_6_out, 1'b1);
  not not_7 (not_7_out, 1'b1);
  not not_8 (not_8_out, 1'b1);
  not not_9 (not_9_out, 1'b1);
  not not_10 (not_10_out, 1'b1);
  not not_11 (not_11_out, 1'b1);
  not not_12 (not_12_out, 1'b1);
  and and_4 (and_4_out, not_3_out, or_1_out);
  and and_5 (and_5_out, not_4_out, or_1_out);
  and and_6 (and_6_out, not_5_out, or_1_out);
  and and_7 (and_7_out, 1'b1, or_2_out);
  and and_8 (and_8_out, not_6_out, or_2_out);
  and and_9 (and_9_out, not_7_out, or_2_out);
  and and_10 (and_10_out, not_8_out, or_3_out);
  and and_11 (and_11_out, 1'b1, or_3_out);
  and and_12 (and_12_out, not_9_out, or_3_out);
  and and_13 (and_13_out, 1'b1, check3_1_o_data);
  and and_14 (and_14_out, 1'b1, check3_1_o_data);
  and and_15 (and_15_out, not_10_out, check3_1_o_data);
  and and_16 (and_16_out, not_11_out, check4_1_o_data);
  and and_17 (and_17_out, not_12_out, check4_1_o_data);
  and and_18 (and_18_out, 1'b1, check4_1_o_data);
  or or_4 (O_DATA[0], and_4_out, and_7_out, and_10_out, and_13_out, and_16_out);
  or or_5 (O_DATA[1], and_5_out, and_8_out, and_11_out, and_14_out, and_17_out);
  or or_6 (O_DATA[2], and_6_out, and_9_out, and_12_out, and_15_out, and_18_out);
endmodule

module sub_stack (
  input  CLK,
  input  RESET,
  input  [1:0] COMMAND,
  input  [2:0] INDEX,
  input  [3:0] I_DATA,
  output [3:0] d0,
  output [3:0] d1,
  output [3:0] d2,
  output [3:0] d3,
  output [3:0] d4,
  output [3:0] O_DATA
);

  wire and_1_out, and_2_out, and_3_out, and_4_out, and_5_out, and_6_out, and_7_out, and_8_out,
       check0_1_o_data, check0_2_o_data, check0_3_o_data, check1_1_o_data, check1_2_o_data, check1_3_o_data,
       check2_1_o_data, check2_2_o_data, check2_3_o_data, check3_1_o_data, check3_2_o_data, check3_3_o_data,
       check4_1_o_data, check4_2_o_data, check4_3_o_data, checker_1_result, checker_2_result,
       checker_3_result, checker_4_result, checker_5_result, not_1_out, not_2_out;
  wire [2:0] convertor_1_o_data, convertor_2_o_data, convertor_minus_1_o_data, indicator_1_o_data,
       indicator_2_o_data, module5_1_o_data;
  wire [3:0] new_and_1_result, new_and_2_result, new_and_3_result, new_and_4_result, new_and_5_result;

  module5 module5_1 (.I_DATA(INDEX), .O_DATA(module5_1_o_data));
  convertor convertor_1 (.ELEMENT1(convertor_minus_1_o_data), .ELEMENT2(module5_1_o_data), .O_DATA(convertor_1_o_data));
  not not_1 (not_1_out, COMMAND[1]);
  not not_2 (not_2_out, COMMAND[0]);
  and and_1 (and_1_out, COMMAND[0], CLK, not_1_out);
  and and_2 (and_2_out, not_2_out, CLK, COMMAND[1]);
  and and_3 (and_3_out, COMMAND[0], CLK, COMMAND[1]);
  check4 check4_1 (.IN_DATA(convertor_1_o_data), .O_DATA(check4_1_o_data));
  check0 check0_1 (.IN_DATA(convertor_1_o_data), .O_DATA(check0_1_o_data));
  check1 check1_1 (.IN_DATA(convertor_1_o_data), .O_DATA(check1_1_o_data));
  check2 check2_1 (.IN_DATA(convertor_1_o_data), .O_DATA(check2_1_o_data));
  check3 check3_1 (.IN_DATA(convertor_1_o_data), .O_DATA(check3_1_o_data));
  indicator indicator_1 (.CLK(and_1_out), .RESET(RESET), .O_DATA(indicator_1_o_data));
  indicator indicator_2 (.CLK(and_3_out), .RESET(RESET), .O_DATA(indicator_2_o_data));
  convertor convertor_2 (.ELEMENT1(indicator_1_o_data), .ELEMENT2(indicator_2_o_data), .O_DATA(convertor_2_o_data));
  convertor_minus convertor_minus_1 (.I_DATA(convertor_2_o_data), .O_DATA(convertor_minus_1_o_data));
  and and_4 (and_4_out, and_3_out, check0_1_o_data);
  and and_5 (and_5_out, and_3_out, check1_1_o_data);
  and and_6 (and_6_out, and_3_out, check2_1_o_data);
  and and_7 (and_7_out, and_3_out, check3_1_o_data);
  and and_8 (and_8_out, and_3_out, check4_1_o_data);
  check0 check0_2 (.IN_DATA(convertor_2_o_data), .O_DATA(check0_2_o_data));
  check1 check1_2 (.IN_DATA(convertor_2_o_data), .O_DATA(check1_2_o_data));
  check2 check2_2 (.IN_DATA(convertor_2_o_data), .O_DATA(check2_2_o_data));
  check3 check3_2 (.IN_DATA(convertor_2_o_data), .O_DATA(check3_2_o_data));
  check4 check4_2 (.IN_DATA(convertor_2_o_data), .O_DATA(check4_2_o_data));
  memory4bit memory4bit_1 (.CLK(and_1_out), .KEY(check0_2_o_data), .RESET(RESET), .I_DATA(I_DATA), .O_DATA(d0));
  check0 check0_3 (.IN_DATA(convertor_minus_1_o_data), .O_DATA(check0_3_o_data));
  \checker  checker_1 (.AND1(check0_3_o_data), .AND2(and_2_out), .OR1(and_4_out), .RESULT(checker_1_result));
  memory4bit memory4bit_2 (.CLK(and_1_out), .KEY(check1_2_o_data), .RESET(RESET), .I_DATA(I_DATA), .O_DATA(d1));
  check1 check1_3 (.IN_DATA(convertor_minus_1_o_data), .O_DATA(check1_3_o_data));
  \checker  checker_2 (.AND1(check1_3_o_data), .AND2(and_2_out), .OR1(and_5_out), .RESULT(checker_2_result));
  memory4bit memory4bit_3 (.CLK(and_1_out), .KEY(check2_2_o_data), .RESET(RESET), .I_DATA(I_DATA), .O_DATA(d2));
  check2 check2_3 (.IN_DATA(convertor_minus_1_o_data), .O_DATA(check2_3_o_data));
  \checker  checker_3 (.AND1(check2_3_o_data), .AND2(and_2_out), .OR1(and_6_out), .RESULT(checker_3_result));
  memory4bit memory4bit_4 (.CLK(and_1_out), .KEY(check3_2_o_data), .RESET(RESET), .I_DATA(I_DATA), .O_DATA(d3));
  check3 check3_3 (.IN_DATA(convertor_minus_1_o_data), .O_DATA(check3_3_o_data));
  \checker  checker_4 (.AND1(check3_3_o_data), .AND2(and_2_out), .OR1(and_7_out), .RESULT(checker_4_result));
  memory4bit memory4bit_5 (.CLK(and_1_out), .KEY(check4_2_o_data), .RESET(RESET), .I_DATA(I_DATA), .O_DATA(d4));
  check4 check4_3 (.IN_DATA(convertor_minus_1_o_data), .O_DATA(check4_3_o_data));
  \checker  checker_5 (.AND1(check4_3_o_data), .AND2(and_2_out), .OR1(and_8_out), .RESULT(checker_5_result));
  new_and new_and_1 (.KEY(checker_1_result), .I_DATA(d0), .RESULT(new_and_1_result));
  new_and new_and_2 (.KEY(checker_2_result), .I_DATA(d1), .RESULT(new_and_2_result));
  new_and new_and_3 (.KEY(checker_3_result), .I_DATA(d2), .RESULT(new_and_3_result));
  new_and new_and_4 (.KEY(checker_4_result), .I_DATA(d3), .RESULT(new_and_4_result));
  new_and new_and_5 (.KEY(checker_5_result), .I_DATA(d4), .RESULT(new_and_5_result));
  result result_1 (
    .d0(new_and_1_result), .d1(new_and_2_result), .d2(new_and_3_result), .d3(new_and_4_result),
    .d4(new_and_5_result), .RES(O_DATA));
endmodule
